# Fritzing sketch design (saved by Fritzing 0.9.3b)
breadboards: 1

parts:
  Part1 = Arduino Uno (Rev3)
  Espessif_Serial_Wifi_Modul_1 = ESP8266 ESP01 [part_number=ESP8266 package=THT]
  DHT1 = DHT11 Humitidy and Temperature Sensor
  R1 = PHOTOCELL [package=photocell-kit]
  YwRobot_Power_Supply1 = YwRobot Breadboard Power Supply [part_number=545043]
  R2 = Resistor [tolerance=±5% resistance=220 package=THT]
  S1 = Pushbutton [package="[THT]"]

nets:
  N1: Part1.A0, R1.P$2, R2.Pin_1
  GND: Part1.GND, Part1.D5_PWM, Espessif_Serial_Wifi_Modul_1.GND, DHT1.GND, YwRobot_Power_Supply1.GND, R2.Pin_0, S1.Pin_1, S1.Pin_2, S1.Pin_3, S1.Pin_4
  N2: Part1.D2, Espessif_Serial_Wifi_Modul_1.RXD
  N3: Part1.D3_PWM, Espessif_Serial_Wifi_Modul_1.TXD
  N4: Part1.D4, DHT1.DATA
  N5: Part1.5V, R1.P$1, YwRobot_Power_Supply1.VCC#9
  VCC: Espessif_Serial_Wifi_Modul_1.VCC, Espessif_Serial_Wifi_Modul_1.GPIO16, Espessif_Serial_Wifi_Modul_1.GPIO00, Espessif_Serial_Wifi_Modul_1.GPIO02, Espessif_Serial_Wifi_Modul_1.CH_PD, DHT1.VDD, YwRobot_Power_Supply1.VCC#5

notes:
  5V
  3.3V

custom parts:
  ESP8266 ESP01: Generic WiFi Module based on the ESP8266 with onboard PCB antenna and UART communications
  DHT11 Humitidy and Temperature Sensor: DHT11 Humidity and Temperature Sensor
  YwRobot Breadboard Power Supply: The YwRobot Breadboard Power Supply (MB-V2) has two power rails; they can be 5V or 3V3. Power to the module can be provided through the female USB socket or through the A10 (female) 2.1mm power jack.
